// Logisim project s-mips.circ as structural Verilog
module S_MIPS_Board (
  input  DESHABILITAR_DISPATCHER,
  output halt
);

  wire button_1_out, CLK, CS, d_ff_1_q, LCLR, LoadRAM, LoadRAMOn, LW, R_R_W, R_W, ram_dispatcher_1_finished,
       RCS, Reset_out, RST, TTY_EN;
  wire [2:0] KDB;
  wire [3:0] LMask, Mask, ram_1_read_time, ram_1_write_time, RMask;
  wire [6:0] KDB_DATA, TTY_DATA;
  wire [15:0] Addr, LAddr, RAddr;
  wire [31:0] I0, I1, I2, I3, LData, ram_1_data_out_0, ram_1_data_out_1, ram_1_data_out_2, ram_1_data_out_3,
       RI0, RI1, RI2, RI3;

  TTY #(.rows(25), .cols(80)) tty_1 (.data(TTY_DATA), .clk(CLK), .we(TTY_EN), .clr(RST));
  not not_1 (LoadRAMOn, ram_dispatcher_1_finished);
  RAM_Dispatcher ram_dispatcher_1 (
    .WriteTime(ram_1_write_time), .Clock(CLK), .Data(LData), .Address(LAddr), .Mask(LMask),
    .Finished(ram_dispatcher_1_finished), .Write(LW), .CLR(LCLR));
  Keyboard #(.buflen(64)) keyboard_1 (.clk(CLK), .re(KDB[0]), .avail(KDB[2]), .data(KDB_DATA));  // open: clr
  RAM ram_1 (
    .Address(RAddr), .Data_Out_0(ram_1_data_out_0), .Data_Out_1(ram_1_data_out_1),
    .Data_Out_2(ram_1_data_out_2), .Data_Out_3(ram_1_data_out_3), .Data_In_0(RI0), .Data_In_1(RI1),
    .Data_In_2(RI2), .Data_In_3(RI3), .Mask(RMask), .nRead_Write(R_R_W), .Chip_Select(RCS),
    .Read_Time(ram_1_read_time), .Reset(button_1_out), .Write_Time(ram_1_write_time));
  Button button_1 (.out(button_1_out));
  D_Flip_Flop d_ff_1 (.clk(CLK), .D(1'b1), .Q(d_ff_1_q), .reset(Reset_out));  // open: Qn, preset, en
  Button Reset (.out(Reset_out));
  S_MIPS s_mips_1 (
    .Kbd_Enable(KDB[0]), .Address(Addr), .Kbd_Clear(KDB[1]), .Kbd_Available(KDB[2]), .RAM_In_0(I0),
    .Kbd_ASCII_Data(KDB_DATA), .RAM_In_1(I1), .TTY_Enable(TTY_EN), .RAM_In_2(I2), .RAM_In_3(I3),
    .TTY_ASCII_Data(TTY_DATA), .Reset(RST), .RAM_Out_0(ram_1_data_out_0), .Clock(CLK),
    .RAM_Out_1(ram_1_data_out_1), .Stop(halt), .RAM_Out_2(ram_1_data_out_2), .RAM_Out_3(ram_1_data_out_3),
    .Mask(Mask), .Read_Time(ram_1_read_time), .Write_Time(ram_1_write_time), .nRead_Write(R_W),
    .Chip_Select(CS));
  D_Flip_Flop d_ff_2 (.clk(CLK), .D(d_ff_1_q), .Qn(LCLR), .reset(Reset_out));  // open: Q, preset, en
  or or_1 (RST, LCLR, LoadRAM);
  Clock clock_1 (.out(CLK));
  Multiplexer #(.width(32), .enable("false")) multiplexer_1 (.in0(I0), .in1(LData), .out(RI0), .sel(LoadRAM));
  Multiplexer #(.width(32), .enable("false")) multiplexer_2 (.in0(I1), .in1(LData), .out(RI1), .sel(LoadRAM));
  Multiplexer #(.width(32), .enable("false")) multiplexer_3 (.in0(I2), .in1(LData), .out(RI2), .sel(LoadRAM));
  Multiplexer #(.width(32), .enable("false")) multiplexer_4 (.in0(I3), .in1(LData), .out(RI3), .sel(LoadRAM));
  and and_1 (LoadRAM, ~DESHABILITAR_DISPATCHER, LoadRAMOn);  // AND_Gate
  Multiplexer #(.width(16), .enable("false")) multiplexer_5 (.in0(Addr), .in1(LAddr), .out(RAddr), .sel(LoadRAM));
  Multiplexer #(.width(4), .enable("false")) multiplexer_6 (.in0(Mask), .in1(LMask), .out(RMask), .sel(LoadRAM));
  Multiplexer #(.enable("false")) multiplexer_7 (.in0(CS), .in1(LW), .out(RCS), .sel(LoadRAM));
  Multiplexer #(.enable("false")) multiplexer_8 (.in0(R_W), .in1(LW), .out(R_R_W), .sel(LoadRAM));

  // Notes on the sheet:
  //   NO MODIFICAR
  //   Keyboard
endmodule

module RAM (
  input  [15:0] Address,
  input  [31:0] Data_In_0,
  input  [31:0] Data_In_1,
  input  [31:0] Data_In_2,
  input  [31:0] Data_In_3,
  input  [3:0] Mask,
  input  nRead_Write,
  input  Chip_Select,
  input  Reset,
  output [31:0] Data_Out_0,
  output [31:0] Data_Out_1,
  output [31:0] Data_Out_2,
  output [31:0] Data_Out_3,
  output [3:0] Read_Time,
  output [3:0] Write_Time
);

  wire and_2_out, and_3_out, and_4_out, and_5_out, and_6_out, and_7_out, and_8_out, and_9_out, Changed, CLK,
       comparator_2_eq, comparator_3_eq, comparator_4_eq, comparator_5_eq, comparator_6_eq, Count,
       demultiplexer_3_out0, Idle, Idle_q, Load, Load0, Load1, nand_1_out, or_1_out, or_2_out, or_3_out,
       or_4_out, or_5_out, or_6_out, or_7_out, or_8_out, or_9_out, or_10_out, Proc_q, Update_Mem, Zero_Time;
  wire [3:0] counter_1_q, multiplexer_1_out, subtractor_1_out;
  wire [31:0] register_1_q, register_2_q, register_3_q, register_4_q, register_5_q;

  // Probe on 4'b0011
  // Probe on 4'b0010
  Multiplexer #(.width(4), .enable("false")) multiplexer_1 (
    .in0(4'b0011), .in1(4'b0010), .out(multiplexer_1_out), .sel(nRead_Write));
  or or_1 (or_1_out, Idle, Update_Mem);
  or or_2 (or_2_out, ~Chip_Select, Reset);  // OR_Gate
  Subtractor #(.width(4)) subtractor_1 (.a(multiplexer_1_out), .b(4'b0010), .out(subtractor_1_out));  // open: bin, bout
  Demultiplexer #(.enable("false")) demultiplexer_1 (.out0(Idle), .out1(Load0), .in(Idle_q), .sel(Changed));
  D_Flip_Flop u_Idle (.clk(CLK), .D(or_1_out), .Q(Idle_q), .preset(or_2_out));  // open: Qn, en, reset
  // Probe on counter_1_q
  Counter #(.width(4), .max('hf)) counter_1 (
    .load(Load), .D(subtractor_1_out), .count(Count), .Q(counter_1_q), .clk(CLK), .clr(or_3_out));  // open: carry
  or or_3 (or_3_out, ~Chip_Select, Reset);  // OR_Gate
  Comparator #(.width(4), .mode("unsigned")) comparator_1 (
    .a(4'b0000), .b(counter_1_q), .eq(Zero_Time));  // open: gt, lt
  or or_4 (or_4_out, Count, Load0, Load1);
  Register #(.width(32)) register_1 (.D(Data_In_0), .en(Chip_Select), .Q(register_1_q), .clk(CLK), .clr(or_5_out));
  or or_5 (or_5_out, ~Chip_Select, Reset);  // OR_Gate
  Register #(.width(32)) register_2 (.D(Data_In_1), .en(Chip_Select), .Q(register_2_q), .clk(CLK), .clr(or_6_out));
  or or_6 (or_6_out, ~Chip_Select, Reset);  // OR_Gate
  Register #(.width(32)) register_3 (.D(Data_In_2), .en(Chip_Select), .Q(register_3_q), .clk(CLK), .clr(or_7_out));
  or or_7 (or_7_out, ~Chip_Select, Reset);  // OR_Gate
  Register #(.width(32)) register_4 (.D(Data_In_3), .en(Chip_Select), .Q(register_4_q), .clk(CLK), .clr(or_8_out));
  or or_8 (or_8_out, ~Chip_Select, Reset);  // OR_Gate
  Register #(.width(32)) register_5 (
    .D({{11{1'b1}}, nRead_Write, Mask, Address}), .en(Chip_Select), .Q(register_5_q), .clk(CLK),
    .clr(or_9_out));
  or or_9 (or_9_out, ~Chip_Select, Reset);  // OR_Gate
  D_Flip_Flop Proc (.clk(CLK), .D(or_4_out), .Q(Proc_q), .reset(or_10_out));  // open: Qn, preset, en
  or or_10 (or_10_out, ~Chip_Select, Reset);  // OR_Gate
  Demultiplexer #(.enable("false")) demultiplexer_2 (
    .out0(Count), .out1(Update_Mem), .in(demultiplexer_3_out0), .sel(Zero_Time));
  Demultiplexer #(.enable("false")) demultiplexer_3 (
    .out0(demultiplexer_3_out0), .out1(Load1), .in(Proc_q), .sel(Changed));
  Clock clock_1 (.out(CLK));
  Comparator #(.width(32)) comparator_2 (.a(register_1_q), .b(Data_In_0), .eq(comparator_2_eq));  // open: gt, lt
  Comparator #(.width(32)) comparator_3 (.a(register_2_q), .b(Data_In_1), .eq(comparator_3_eq));  // open: gt, lt
  Comparator #(.width(32)) comparator_4 (.a(register_3_q), .b(Data_In_2), .eq(comparator_4_eq));  // open: gt, lt
  Comparator #(.width(32)) comparator_5 (.a(register_4_q), .b(Data_In_3), .eq(comparator_5_eq));  // open: gt, lt
  Comparator #(.width(32)) comparator_6 (
    .a(register_5_q), .b({{11{1'b1}}, nRead_Write, Mask, Address}), .eq(comparator_6_eq));  // open: gt, lt
  nand nand_1 (nand_1_out, comparator_6_eq, comparator_2_eq, comparator_3_eq, comparator_4_eq, comparator_5_eq);
  and and_1 (Changed, nand_1_out, Chip_Select);
  or or_11 (Load, Count, Load1, Load0);
  and and_2 (and_2_out, Mask[0], Update_Mem, nRead_Write);
  and and_3 (and_3_out, Mask[1], Update_Mem, nRead_Write);
  and and_4 (and_4_out, Mask[2], Update_Mem, nRead_Write);
  and and_5 (and_5_out, Mask[3], Update_Mem, nRead_Write);
  RAM_part #(.addrWidth(16), .dataWidth(32), .bus("separate")) ram_1 (
    .addr(Address), .din(Data_In_0), .data(Data_Out_0), .str(and_2_out), .sel(Chip_Select), .clk(CLK),
    .ld(and_6_out), .clr(Reset));
  and and_6 (and_6_out, ~nRead_Write, Idle);  // AND_Gate
  RAM_part #(.addrWidth(16), .dataWidth(32), .bus("separate")) ram_2 (
    .addr(Address), .din(Data_In_1), .data(Data_Out_1), .str(and_3_out), .sel(Chip_Select), .clk(CLK),
    .ld(and_7_out), .clr(Reset));
  and and_7 (and_7_out, ~nRead_Write, Idle);  // AND_Gate
  RAM_part #(.addrWidth(16), .dataWidth(32), .bus("separate")) ram_3 (
    .addr(Address), .din(Data_In_2), .data(Data_Out_2), .str(and_4_out), .sel(Chip_Select), .clk(CLK),
    .ld(and_8_out), .clr(Reset));
  and and_8 (and_8_out, ~nRead_Write, Idle);  // AND_Gate
  RAM_part #(.addrWidth(16), .dataWidth(32), .bus("separate")) ram_4 (
    .addr(Address), .din(Data_In_3), .data(Data_Out_3), .str(and_5_out), .sel(Chip_Select), .clk(CLK),
    .ld(and_9_out), .clr(Reset));
  and and_9 (and_9_out, ~nRead_Write, Idle);  // AND_Gate

  assign Read_Time = 4'b0011;
  assign Write_Time = 4'b0010;

  // Other names for the same wires on the sheet: M0 = Mask[0]; M1 = Mask[1]; M2 = Mask[2]; M3 = Mask[3];
  //   RW = nRead_Write; CLR = Reset; CS = Chip_Select; Load2 = Count

  // Notes on the sheet:
  //   NO MODIFICAR
  //   excepto quizás los valores RT y WT
  //   BANK0
  //   BANK1
  //   BANK2
  //   BANK3
endmodule

module RAM_Dispatcher (
  input  [3:0] WriteTime,
  input  Clock,
  input  CLR,
  output [31:0] Data,
  output [15:0] Address,
  output [3:0] Mask,
  output Finished,
  output Write
);

  wire demultiplexer_2_out1, demultiplexer_3_out1, End, IDLE_q, IncAddr, Load, or_1_out, or_2_out, While_q,
       WriteEnd;
  wire [3:0] counter_1_q;
  wire [31:0] CurrentAddress_q;

  Counter #(.width(32), .max('hffffffff)) CurrentAddress (
    .count(IncAddr), .Q({CurrentAddress_q[31:18], Address, CurrentAddress_q[1:0]}), .clk(Clock), .clr(CLR));  // open: load, D, carry
  or or_1 (or_1_out, IncAddr, demultiplexer_3_out1, Finished);
  D_Flip_Flop IDLE (.clk(Clock), .D(or_1_out), .Q(IDLE_q), .preset(CLR));  // open: Qn, en, reset
  Demultiplexer #(.enable("false")) demultiplexer_1 (.out0(Load), .out1(Finished), .in(IDLE_q), .sel(End));
  D_Flip_Flop While (.clk(Clock), .D(or_2_out), .Q(While_q), .reset(CLR));  // open: Qn, preset, en
  or or_2 (or_2_out, Write, Load);
  RAM_part #(.addrWidth(18), .dataWidth(32)) ram_1 (
    .addr({Address, CurrentAddress_q[1:0]}), .data(Data), .clk(Clock));  // open: sel, ld, clr
  Demultiplexer #(.enable("false")) demultiplexer_2 (
    .out0(Write), .out1(demultiplexer_2_out1), .in(While_q), .sel(WriteEnd));
  Decoder #(.select(2)) decoder_1 (
    .out0(Mask[0]), .out1(Mask[1]), .out2(Mask[2]), .out3(Mask[3]), .sel(CurrentAddress_q[1:0]));  // open: en
  Demultiplexer #(.enable("false")) demultiplexer_3 (
    .out0(IncAddr), .out1(demultiplexer_3_out1), .in(demultiplexer_2_out1), .sel(End));
  Counter #(.width(4), .max('hf)) counter_1 (
    .load(Load), .D(WriteTime), .count(Write), .Q(counter_1_q), .clk(Clock));  // open: carry, clr
  Comparator #(.width(32)) comparator_1 (.a(Data), .b({32{1'b1}}), .eq(End));  // open: gt, lt
  Comparator #(.width(4)) comparator_2 (.a(4'b0000), .b(counter_1_q), .eq(WriteEnd));  // open: gt, lt

  // Other names for the same wires on the sheet: CLK = Clock; Count = Write; WT[3:0] = WriteTime
endmodule

module S_MIPS (
  input  [31:0] RAM_Out_0,
  input  [31:0] RAM_Out_1,
  input  Kbd_Available,
  input  Reset,
  input  [6:0] Kbd_ASCII_Data,
  input  [31:0] RAM_Out_2,
  input  Clock,
  input  [31:0] RAM_Out_3,
  input  [3:0] Read_Time,
  input  [3:0] Write_Time,
  output [31:0] RAM_In_0,
  output TTY_Enable,
  output Kbd_Enable,
  output [6:0] TTY_ASCII_Data,
  output Kbd_Clear,
  output [31:0] RAM_In_1,
  output [31:0] RAM_In_2,
  output Stop,
  output [31:0] RAM_In_3,
  output [15:0] Address,
  output nRead_Write,
  output Chip_Select,
  output [3:0] Mask
);

  wire branch_control_1_out_12, control_unit_1_alu_a_selector, control_unit_1_save_alu_result,
       control_unit_1_take_direct_alu_op, control_unit_1_write_rf, control_unit_1_write_sp, Equals,
       instruction_decoder_1_inmediate, instruction_decoder_1_jmp, instruction_decoder_1_nhi_lo,
       instruction_decoder_1_npush_pop, instruction_decoder_1_nread_write,
       instruction_decoder_1_nread_write_memory, instruction_decoder_1_write_rd, Stack, try_jmp, Update_PC,
       Wl;
  wire [1:0] Addr, control_unit_1_alu_b_selector, instruction_decoder_1_jump_value_selector;
  wire [2:0] control_unit_1_data_in_selector, instruction_decoder_1_jump_type,
       instruction_decoder_1_operation_type;
  wire [4:0] instruction_decoder_1_rd, instruction_decoder_1_rs, instruction_decoder_1_rt;
  wire [5:0] instruction_decoder_1_func_code, instruction_decoder_1_op_code;
  wire [15:0] instruction_decoder_1_offset;
  wire [31:0] ALU_out, ALU_res, instruction_decoder_1_jump_value, multiplexer_1_out, multiplexer_2_out,
       n16_to_32_bit_extender_1_out, n16_to_32_bit_extender_1_outx4, PC, Ram_Out, RF_B;
  wire [31:7] RF_A;

  Instruction_decoder instruction_decoder_1 (
    .Instruction(Ram_Out), .Write_Instruction(Wl), .Clock(Clock), .Reset(Reset),
    .Program_Counter__updated(PC), .Write_Rd(instruction_decoder_1_write_rd),
    .jmp(instruction_decoder_1_jmp), .Offset(instruction_decoder_1_offset),
    .nRead_Write(instruction_decoder_1_nread_write), .Op_Code(instruction_decoder_1_op_code),
    .Jump_Value_Selector(instruction_decoder_1_jump_value_selector), .Rs(instruction_decoder_1_rs),
    .Func_Code(instruction_decoder_1_func_code), .Rd(instruction_decoder_1_rd),
    .Rt(instruction_decoder_1_rt), .Jump_Value(instruction_decoder_1_jump_value),
    .Inmediate(instruction_decoder_1_inmediate), .nHi_Lo(instruction_decoder_1_nhi_lo),
    .Operation_Type(instruction_decoder_1_operation_type), .nPush_Pop(instruction_decoder_1_npush_pop),
    .nRead_Write_Memory(instruction_decoder_1_nread_write_memory), .Jump_Type(instruction_decoder_1_jump_type));
  Multiplexer #(.select(2), .width(32), .enable("false")) multiplexer_1 (
    .in0(instruction_decoder_1_jump_value), .in1(ALU_res), .in2({RF_A, TTY_ASCII_Data}),
    .out(multiplexer_1_out), .sel(instruction_decoder_1_jump_value_selector));  // open: in3
  // Probe on instruction_decoder_1_operation_type
  Branch_Control branch_control_1 (
    .Jump_Operation(instruction_decoder_1_jmp), .Jump_Selector(instruction_decoder_1_jump_type),
    .Next_Program_Counter_Value(ALU_res), .ALU_Less(ALU_out[0]), .ALU_Equals(Equals), .Update_PC(Update_PC),
    .Jump_Value(multiplexer_1_out), .Program_Counter(PC), .Reset(Reset), .out_12(branch_control_1_out_12),
    .Clock(Clock), .Try_Jump(try_jmp));
  _16_to_32_bit_extender u_16_to_32_bit_extender_1 (
    .In(instruction_decoder_1_offset), .Out(n16_to_32_bit_extender_1_out),
    .Outx4(n16_to_32_bit_extender_1_outx4));
  // Probe on Update_PC
  Control_Unit control_unit_1 (
    .Start(1'b1), .Immediate(instruction_decoder_1_inmediate), .Reset(Reset),
    .nLo_Hi(instruction_decoder_1_nhi_lo), .Clock(Clock), .nPush_Pop(instruction_decoder_1_npush_pop),
    .Operation(instruction_decoder_1_operation_type), .kbd_Available(Kbd_Available),
    .nR_W_Mem(instruction_decoder_1_nread_write_memory), .Read_Ram(Read_Time), .Write_Ram(Write_Time),
    .End(Stop), .TTY_Enable(TTY_Enable), .Keyboard_Enable(Kbd_Enable), .Access_SP(Stack),
    .ALU_A_Selector(control_unit_1_alu_a_selector), .Write_SP(control_unit_1_write_sp),
    .Data_In_Selector(control_unit_1_data_in_selector), .ALU_B_Selector(control_unit_1_alu_b_selector),
    .Write_RF(control_unit_1_write_rf), .Save_ALU_Result(control_unit_1_save_alu_result),
    .Take_Direct_ALU_Op(control_unit_1_take_direct_alu_op), .Write_Instruction(Wl), .Update_PC(Update_PC),
    .Try_jump(try_jmp), .Chip_Select(Chip_Select), .RAM_Address_Selector(Addr), .Write_Ram_2(nRead_Write));
  Multiplexer #(.select(2), .width(32), .enable("false")) multiplexer_2 (
    .in0(PC), .in1(ALU_res), .in2({RF_A, TTY_ASCII_Data}), .out(multiplexer_2_out), .sel(Addr));  // open: in3
  Access_Memory access_memory_1 (
    .Target_Address(multiplexer_2_out), .Ram_O0(RAM_Out_0), .Ram_O1(RAM_Out_1), .To_Write(RF_B),
    .Ram_O2(RAM_Out_2), .Ram_O3(RAM_Out_3), .Address(Address), .Mask(Mask), .Ram_I0(RAM_In_0),
    .Ram_I1(RAM_In_1), .Ram_out(Ram_Out), .Ram_I2(RAM_In_2), .Ram_I3(RAM_In_3));
  Data_Path data_path_1 (
    .Rs(instruction_decoder_1_rs), .ALU_A_Selector(control_unit_1_alu_a_selector), .Memory_Input(Ram_Out),
    .Rt(instruction_decoder_1_rt), .ALU_B_Selector(control_unit_1_alu_b_selector),
    .Rd(instruction_decoder_1_rd), .KBD_Data(Kbd_ASCII_Data),
    .Save_ALU_Result(control_unit_1_save_alu_result), .RW(instruction_decoder_1_nread_write),
    .nRt_Rd(instruction_decoder_1_write_rd), .ALU_Sum(control_unit_1_take_direct_alu_op), .Reset(Reset),
    .Op_Code(instruction_decoder_1_op_code), .Clock(Clock), .Func_Code(instruction_decoder_1_func_code),
    .Write_Reg_File(control_unit_1_write_rf), .Access_SP(Stack), .Offset(n16_to_32_bit_extender_1_out),
    .Program_Counter(PC), .DI_Selector(control_unit_1_data_in_selector),
    .Offset_x4(n16_to_32_bit_extender_1_outx4), .Write_SP(control_unit_1_write_sp),
    .Compare_to_Zero(branch_control_1_out_12), .out_24(Equals), .RF_A({RF_A, TTY_ASCII_Data}),
    .ALU_out(ALU_out), .RF_B(RF_B), .ALU_Result(ALU_res));

  // Other names for the same wires on the sheet: CLK = Clock; CLR = Reset; CS = Chip_Select;
  //   KBD_AVAIL = Kbd_Available; KBD_CLR = Kbd_Clear; KBD_DATA[6:0] = Kbd_ASCII_Data; RAM_A[15:0] = Address;
  //   RAM_INPUT_0[31:0] = RAM_In_0; RAM_INPUT_1[31:0] = RAM_In_1; RAM_INPUT_2[31:0] = RAM_In_2;
  //   RAM_INPUT_3[31:0] = RAM_In_3; RAM_MASK[3:0] = Mask; RAM_OUTPUT_0[31:0] = RAM_Out_0;
  //   RAM_OUTPUT_1[31:0] = RAM_Out_1; RAM_OUTPUT_2[31:0] = RAM_Out_2; RAM_OUTPUT_3[31:0] = RAM_Out_3;
  //   RF_A[6:0] = TTY_ASCII_Data; TTY_DATA[6:0] = TTY_ASCII_Data; RW = nRead_Write

  // Notes on the sheet:
  //   Inputs
  //   DATA FROM RAM
  //   RAM TIMING
  //   Ram
  //   Outputs
  //   DATA TO RAM
  //   RAM ADDRESS
  //   DATA WRITE MASK
  //   RAM CONTROL
  //   KEYBOARD
  //   Misc
  //   TTY
  //   SEQUENCING
endmodule

module Control_Unit (
  input  Start,
  input  Immediate,
  input  Reset,
  input  nLo_Hi,
  input  Clock,
  input  nPush_Pop,
  input  [2:0] Operation,
  input  kbd_Available,
  input  nR_W_Mem,
  input  [3:0] Read_Ram,
  input  [3:0] Write_Ram,
  output End,
  output TTY_Enable,
  output Keyboard_Enable,
  output Access_SP,
  output ALU_A_Selector,
  output [2:0] Data_In_Selector,
  output [1:0] ALU_B_Selector,
  output Write_SP,
  output Write_RF,
  output Save_ALU_Result,
  output Take_Direct_ALU_Op,
  output Try_jump,
  output Update_PC,
  output Write_Instruction,
  output Chip_Select,
  output [1:0] RAM_Address_Selector,
  output Write_Ram_2
);

  wire ALU_4_2, ALU_A_1, ALU_A_3, ALU_B_1, ALU_OS_1, ALU_OSx4, and_1_out, and_2_out, and_3_out, and_4_out,
       and_5_out, chronometer_1_out_6, CLK_CHR, demultiplexer_1_out0, demultiplexer_1_out1,
       demultiplexer_2_out0, demultiplexer_2_out1, demultiplexer_2_out2, demultiplexer_2_out3,
       demultiplexer_2_out4, demultiplexer_2_out5, demultiplexer_2_out6, demultiplexer_2_out7, End_Inst, mem,
       Memory_2, minus_1, or_1_out, or_2_out, or_5_out, or_6_out, or_8_out, or_9_out, or_10_out, or_15_out,
       preF, S2__Read_RF__char_q, S2__Read_RF__operators_3_q, S2__Read_RF__operators_q,
       S2__Read_RF__SP___Rs_q, S5__Wait_for_Memory_q, S9__Read_kbd_buffer_q, S10__End_q, S11__IDLE_q, SP,
       WHi, WLo, WRF_4;
  wire [3:0] Mem_Time, multiplexer_1_out;

  D_Flip_Flop #(.trigger("falling")) S10__End (
    .clk(Clock), .D(demultiplexer_2_out7), .Q(S10__End_q), .en(or_1_out), .reset(Reset));  // open: Qn, preset
  or or_1 (or_1_out, demultiplexer_2_out7, Reset);
  Multiplexer #(.width(4), .enable("false")) multiplexer_1 (
    .in0(Mem_Time), .in1(Read_Ram), .out(multiplexer_1_out), .sel(Write_Instruction));
  Multiplexer #(.width(4), .enable("false")) multiplexer_2 (
    .in0(Read_Ram), .in1(Write_Ram), .out(Mem_Time), .sel(nR_W_Mem));
  D_Flip_Flop #(.trigger("falling")) S11__IDLE (
    .clk(Clock), .D(S10__End_q), .Q(S11__IDLE_q), .preset(Reset));  // open: Qn, en, reset
  or or_2 (or_2_out, ALU_A_3, preF, ALU_4_2);
  and and_1 (and_1_out, S11__IDLE_q, Start);
  or or_3 (preF, and_1_out, End_Inst);
  Chronometer chronometer_1 (
    .INPUTS(Clock), .in_2(1'b1), .in_3(multiplexer_1_out), .in_4(or_2_out), .out_6(chronometer_1_out_6));  // open: out_5
  D_Flip_Flop #(.trigger("falling")) S0__Fetch (
    .clk(CLK_CHR), .D(preF), .Q(Write_Instruction), .reset(Reset));  // open: Qn, preset, en
  or or_4 (End, demultiplexer_2_out7, S10__End_q);
  Multiplexer #(.enable("false")) multiplexer_3 (.in0(Clock), .in1(chronometer_1_out_6), .out(CLK_CHR), .sel(or_5_out));
  or or_5 (or_5_out, mem, Write_Instruction, Memory_2);
  D_Flip_Flop #(.trigger("falling")) S1__Decode (
    .clk(CLK_CHR), .D(Write_Instruction), .Q(Update_PC), .reset(Reset));  // open: Qn, preset, en
  Demultiplexer #(.enable("false")) demultiplexer_1 (
    .out0(demultiplexer_1_out0), .out1(demultiplexer_1_out1), .in(Memory_2), .sel(nPush_Pop));
  Demultiplexer #(.select(3), .enable("false")) demultiplexer_2 (
    .out0(demultiplexer_2_out0), .out1(demultiplexer_2_out1), .out2(demultiplexer_2_out2),
    .out3(demultiplexer_2_out3), .out4(demultiplexer_2_out4), .out5(demultiplexer_2_out5),
    .out6(demultiplexer_2_out6), .out7(demultiplexer_2_out7), .in(Update_PC), .sel(Operation));
  or or_6 (or_6_out, mem, demultiplexer_1_out0);
  or or_7 (ALU_A_Selector, ALU_A_1, Try_jump, ALU_A_3, ALU_4_2);
  or or_8 (or_8_out, ALU_B_1, Try_jump);
  or or_9 (or_9_out, Write_Instruction, ALU_4_2);
  or or_10 (or_10_out, ALU_OS_1, ALU_A_3);
  or or_11 (Save_ALU_Result, Write_Instruction, ALU_OSx4, ALU_A_3, ALU_4_2);
  or or_12 (Take_Direct_ALU_Op, Write_Instruction, ALU_OSx4, ALU_A_3);
  or or_13 (Chip_Select, mem, Write_Instruction, Memory_2);
  Priority_Encoder #(.select(2)) priority_encoder_1 (
    .in0(1'b1), .in1(or_6_out), .in2(demultiplexer_1_out1), .out(RAM_Address_Selector));  // open: in3, gs, en_out, en_in
  and and_2 (and_2_out, Memory_2, ~nPush_Pop);  // AND_Gate
  and and_3 (and_3_out, nR_W_Mem, mem);
  Priority_Encoder #(.select(2)) priority_encoder_2 (
    .in0(1'b1), .in1(or_9_out), .in2(or_10_out), .in3(ALU_OSx4), .out(ALU_B_Selector));  // open: gs, en_out, en_in
  or or_14 (Write_Ram_2, and_2_out, and_3_out);
  D_Flip_Flop #(.trigger("falling")) S2__Read_RF__operators (
    .clk(Clock), .D(demultiplexer_2_out0), .Q(S2__Read_RF__operators_q), .reset(Reset));  // open: Qn, preset, en
  D_Flip_Flop #(.trigger("falling")) S2__Read_RF__operators_2 (
    .clk(Clock), .D(demultiplexer_2_out1), .Q(ALU_OSx4), .reset(Reset));  // open: Qn, preset, en
  D_Flip_Flop #(.trigger("falling")) S2__Read_RF__operators_3 (
    .clk(Clock), .D(demultiplexer_2_out2), .Q(S2__Read_RF__operators_3_q), .reset(Reset));  // open: Qn, preset, en
  D_Flip_Flop #(.trigger("falling")) S6__Write__from_Hi_Lo (
    .clk(Clock), .D(demultiplexer_2_out3), .Q(WRF_4), .reset(Reset));  // open: Qn, preset, en
  D_Flip_Flop #(.trigger("falling")) S2__Read_RF__char (
    .clk(Clock), .D(demultiplexer_2_out5), .Q(S2__Read_RF__char_q), .reset(Reset));  // open: Qn, preset, en
  D_Flip_Flop #(.trigger("falling")) S9__Read_kbd_buffer (
    .clk(Clock), .D(demultiplexer_2_out6), .Q(S9__Read_kbd_buffer_q), .reset(Reset));  // open: Qn, preset, en
  D_Flip_Flop #(.trigger("falling")) S3__Operate_and_Write (
    .clk(Clock), .D(S2__Read_RF__operators_q), .Q(ALU_A_1), .reset(Reset));  // open: Qn, preset, en
  D_Flip_Flop #(.trigger("falling")) S3__Operate_and_Write_2 (
    .clk(Clock), .D(ALU_OSx4), .Q(Try_jump), .reset(Reset));  // open: Qn, preset, en
  D_Flip_Flop #(.trigger("falling")) S3__Operate_and_Write_3 (
    .clk(Clock), .D(S2__Read_RF__operators_3_q), .Q(ALU_A_3), .reset(Reset));  // open: Qn, preset, en
  Demultiplexer #(.enable("false")) demultiplexer_3 (.out0(WLo), .out1(WHi), .in(WRF_4), .sel(nLo_Hi));
  D_Flip_Flop #(.trigger("falling")) S2__Read_RF__SP___Rs (
    .clk(Clock), .D(demultiplexer_2_out4), .Q(S2__Read_RF__SP___Rs_q), .reset(Reset));  // open: Qn, preset, en
  D_Flip_Flop #(.trigger("falling")) S8__Write_in_terminal (
    .clk(Clock), .D(S2__Read_RF__char_q), .Q(TTY_Enable), .reset(Reset));  // open: Qn, preset, en
  Demultiplexer #(.enable("false")) demultiplexer_4 (.out0(ALU_B_1), .out1(ALU_OS_1), .in(ALU_A_1), .sel(Immediate));
  Demultiplexer #(.enable("false")) demultiplexer_5 (
    .out0(minus_1), .out1(Keyboard_Enable), .in(S9__Read_kbd_buffer_q), .sel(kbd_Available));
  or or_15 (or_15_out, mem, Memory_2);
  and and_4 (and_4_out, mem, ~nR_W_Mem);  // AND_Gate
  and and_5 (and_5_out, Memory_2, nPush_Pop);
  D_Flip_Flop #(.trigger("falling")) S4__Access_Memory (
    .clk(CLK_CHR), .D(ALU_A_3), .Q(mem), .reset(Reset));  // open: Qn, preset, en
  D_Flip_Flop #(.trigger("falling")) S3__Operate_and_Write_4 (
    .clk(Clock), .D(S2__Read_RF__SP___Rs_q), .Q(ALU_4_2), .reset(Reset));  // open: Qn, preset, en
  or or_16 (Access_SP, SP, Memory_2);
  Priority_Encoder priority_encoder_3 (
    .in0(1'b1), .in1(Write_SP), .in2(WHi), .in3(WLo), .in4(or_15_out), .in5(Keyboard_Enable), .in6(minus_1),
    .out(Data_In_Selector));  // open: in7, en_in, gs, en_out
  or or_17 (Write_RF, ALU_A_1, and_4_out, WRF_4, and_5_out);
  or or_18 (SP, ALU_4_2, S2__Read_RF__SP___Rs_q);
  D_Flip_Flop #(.trigger("falling")) S5__Wait_for_Memory (
    .clk(CLK_CHR), .D(mem), .Q(S5__Wait_for_Memory_q), .reset(Reset));  // open: Qn, preset, en
  D_Flip_Flop #(.trigger("falling")) S4__Access_Memory_2 (
    .clk(CLK_CHR), .D(ALU_4_2), .Q(Memory_2), .reset(Reset));  // open: Qn, preset, en
  D_Flip_Flop #(.trigger("falling")) S5__Wait_for_Memory_2 (
    .clk(CLK_CHR), .D(Memory_2), .Q(Write_SP), .reset(Reset));  // open: Qn, preset, en
  or or_19 (End_Inst, ALU_A_1, Try_jump, S5__Wait_for_Memory_q, WRF_4, Write_SP, TTY_Enable, S9__Read_kbd_buffer_q);

  // Other names for the same wires on the sheet: ALU_4_1 = Write_Instruction; ALU_PC_1 = Write_Instruction;
  //   fetch = Write_Instruction; Save_ALU_1 = Write_Instruction; TD_1 = Write_Instruction; Wl = Write_Instruction;
  //   Hi = nLo_Hi; Imm = Immediate; ALU_A_2 = Try_jump; ALU_B_2 = Try_jump; jmp = Try_jump; kbd_A = kbd_Available;
  //   KBD_in = Keyboard_Enable; Memory_1 = mem; WRF_3 = mem; OP[2:0] = Operation; Pop = nPush_Pop; ALU_OS_2 = ALU_A_3;
  //   preM = ALU_A_3; Save_ALU_3 = ALU_A_3; ALU_A_4 = ALU_4_2; preS = ALU_4_2; Save_ALU_4 = ALU_4_2;
  //   Read_Time[3:0] = Read_Ram; RST = Reset; stack = Memory_2; WRF_5 = Memory_2; ALU_PC_2 = ALU_OSx4;
  //   Save_ALU_2 = ALU_OSx4; TD_2 = ALU_OSx4; UD_PC_1 = Update_PC; ALU_out = ALU_A_1; WRF_1 = ALU_A_1;
  //   ALU_res = Write_SP; WSP = Write_SP

  // Notes on the sheet:
  //   Inputs
  //   Memory Clock
  //   Control Signals
  //   Halt
  //   ALU Operation
  //   Jump operation
  //   Memory Operation
  //   Move Operation
  //   ALU Signals
  //   Memory Signals
  //   Stack operation
  //   Write in terminal
  //   Read Keyboard
  //   Outputs
  //   RF Signals
  //   Misc Signals
endmodule

module Data_Path (
  input  [4:0] Rs,
  input  ALU_A_Selector,
  input  [31:0] Memory_Input,
  input  [4:0] Rt,
  input  [1:0] ALU_B_Selector,
  input  [4:0] Rd,
  input  [6:0] KBD_Data,
  input  Save_ALU_Result,
  input  RW,
  input  nRt_Rd,
  input  ALU_Sum,
  input  Reset,
  input  [5:0] Op_Code,
  input  Clock,
  input  [5:0] Func_Code,
  input  Write_Reg_File,
  input  Access_SP,
  input  [31:0] Offset,
  input  [31:0] Program_Counter,
  input  [2:0] DI_Selector,
  input  [31:0] Offset_x4,
  input  Write_SP,
  input  Compare_to_Zero,
  output out_24,
  output [31:0] RF_A,
  output [31:0] ALU_out,
  output [31:0] RF_B,
  output [31:0] ALU_Result
);

  wire alu_decoder_1_write_hi___lo, and_1_out, or_1_out, WH_L;
  wire [3:0] alu_decoder_1_alu_operation;
  wire [4:0] multiplexer_2_out, multiplexer_3_out, multiplexer_4_out, multiplexer_4_out_2;
  wire [31:0] bit_extender_1_out, Hi, HI__in, Lo, multiplexer_1_out, multiplexer_5_out, multiplexer_6_out,
       multiplexer_7_out;

  // Probe on Rs
  // Probe on Rt
  // Probe on Rd
  assign bit_extender_1_out = {{25{KBD_Data[6]}}, KBD_Data};  // Bit_Extender bit_extender_1
  Multiplexer #(.select(3), .width(32), .enable("false")) multiplexer_1 (
    .in0(ALU_out), .in1(ALU_Result), .in2(Hi), .in3(Lo), .in4(Memory_Input), .in5(bit_extender_1_out),
    .in6({32{1'b1}}), .out(multiplexer_1_out), .sel(DI_Selector));  // open: in7
  and and_1 (and_1_out, RW, ~WH_L, Write_Reg_File);  // AND_Gate
  Multiplexer #(.width(5), .enable("false")) multiplexer_2 (.in0(Rt), .in1(Rd), .out(multiplexer_2_out), .sel(nRt_Rd));
  Multiplexer #(.width(5), .enable("false")) multiplexer_3 (
    .in0(multiplexer_2_out), .in1({5{1'b1}}), .out(multiplexer_3_out), .sel(Write_SP));
  or or_1 (or_1_out, and_1_out, Write_SP);
  Register_File register_file_1 (
    .in_1(multiplexer_4_out_2), .in_3(multiplexer_4_out), .in_4(multiplexer_3_out), .in_6(or_1_out),
    .in_7(Clock), .in_8(Reset), .in_10(WH_L), .R1(RF_A), .R2(RF_B), .in_2(HI__in), .in_5(ALU_out),
    .in_9(multiplexer_1_out), .HI_Out(Hi), .LO_Out(Lo));
  Multiplexer #(.width(10), .enable("false")) multiplexer_4 (
    .in0({Rs, Rt}), .in1({{5{1'b1}}, Rs}), .out({multiplexer_4_out_2, multiplexer_4_out}), .sel(Access_SP));
  // Probe on multiplexer_4_out_2
  // Probe on RF_A
  // Probe on RF_B
  // Probe on multiplexer_4_out
  // Probe on Program_Counter
  Multiplexer #(.width(32), .enable("false")) multiplexer_5 (
    .in0(Program_Counter), .in1(RF_A), .out(multiplexer_5_out), .sel(ALU_A_Selector));
  Multiplexer #(.width(32), .enable("false")) multiplexer_6 (
    .in0(RF_B), .in1({32{1'b0}}), .out(multiplexer_6_out), .sel(Compare_to_Zero));
  Multiplexer #(.select(2), .width(32), .enable("false")) multiplexer_7 (
    .in0(multiplexer_6_out), .in1(32'h4), .in2(Offset), .in3(Offset_x4), .out(multiplexer_7_out),
    .sel(ALU_B_Selector));
  ALU alu_1 (
    .in_1(alu_decoder_1_alu_operation), .Equal(out_24), .in_2(multiplexer_5_out), .in_3(multiplexer_7_out),
    .out_6(ALU_out), .out_7(HI__in));  // open: Carry_Flag, Overflow, Zero_Flag
  ALU_Decoder alu_decoder_1 (
    .Op_Code(Op_Code), .Func_Code(Func_Code), .Sum(ALU_Sum), .ALU_Operation(alu_decoder_1_alu_operation),
    .Write_Hi___Lo(alu_decoder_1_write_hi___lo));
  // Probe on ALU_out
  and and_2 (WH_L, Write_Reg_File, alu_decoder_1_write_hi___lo);
  Register #(.width(32), .trigger("falling")) register_1 (
    .D(ALU_out), .en(Save_ALU_Result), .Q(ALU_Result), .clk(Clock), .clr(Reset));

  // Other names for the same wires on the sheet: A[31:0] = RF_A; A_Sel = ALU_A_Selector; Acc_SP = Access_SP;
  //   B[31:0] = RF_B; B_Sel[1:0] = ALU_B_Selector; CLK = Clock; DI_Sel[2:0] = DI_Selector; Equal = out_24;
  //   FC[5:0] = Func_Code; LO__in[31:0] = ALU_out; Mem_In[31:0] = Memory_Input; OC[5:0] = Op_Code; Os[31:0] = Offset;
  //   Os_x4[31:0] = Offset_x4; PC[31:0] = Program_Counter; RST = Reset; Save_ALU = Save_ALU_Result; tunnel = ALU_Sum;
  //   WRF = Write_Reg_File; WSP = Write_SP; Zero = Compare_to_Zero

  // Notes on the sheet:
  //   Branch Control
  //   INPUTS
  //   OUTPUTS
endmodule

module Register_File (
  input  [4:0] in_1,
  input  [31:0] in_2,
  input  [4:0] in_3,
  input  [4:0] in_4,
  input  [31:0] in_5,
  input  in_6,
  input  in_7,
  input  in_8,
  input  [31:0] in_9,
  input  in_10,
  output [31:0] R1,
  output [31:0] HI_Out,
  output [31:0] R2,
  output [31:0] LO_Out
);

  wire decoder_1_out0, decoder_1_out1, decoder_1_out2, decoder_1_out3, decoder_2_out0, decoder_2_out1,
       decoder_2_out2, decoder_2_out3, decoder_2_out4, decoder_2_out5, decoder_2_out6, decoder_2_out7,
       decoder_3_out0, decoder_3_out1, decoder_3_out2, decoder_3_out3, decoder_3_out4, decoder_3_out5,
       decoder_3_out6, decoder_3_out7, decoder_4_out0, decoder_4_out1, decoder_4_out2, decoder_4_out3,
       decoder_4_out4, decoder_4_out5, decoder_4_out6, decoder_4_out7, decoder_5_out0, decoder_5_out1,
       decoder_5_out2, decoder_5_out3, decoder_5_out4, decoder_5_out5, decoder_5_out6, decoder_5_out7;
  wire [31:0] _00, _01, _02, _03, _04, _05, _06, _07, _08, _09, _10, _11, _12, _13, _14, _15, _16, _17, _18,
       _19, _20, _21, _22, _23, _24, _25, _26, _27, _28, _29, _30, _31;

  Register #(.width(32), .trigger("falling")) register_1 (.D(in_2), .en(in_10), .Q(HI_Out), .clk(in_7), .clr(in_8));
  Register #(.width(32), .trigger("falling")) register_2 (.D(in_5), .en(in_10), .Q(LO_Out), .clk(in_7), .clr(in_8));
  Decoder #(.select(2), .disabled(0)) decoder_1 (
    .out0(decoder_1_out0), .out1(decoder_1_out1), .out2(decoder_1_out2), .out3(decoder_1_out3),
    .sel(in_4[4:3]), .en(in_6));
  Decoder #(.select(3), .disabled(0)) decoder_2 (
    .out0(decoder_2_out0), .out1(decoder_2_out1), .out2(decoder_2_out2), .out3(decoder_2_out3),
    .out4(decoder_2_out4), .out5(decoder_2_out5), .out6(decoder_2_out6), .out7(decoder_2_out7),
    .sel(in_4[2:0]), .en(decoder_1_out0));
  Decoder #(.select(3), .disabled(0)) decoder_3 (
    .out0(decoder_3_out0), .out1(decoder_3_out1), .out2(decoder_3_out2), .out3(decoder_3_out3),
    .out4(decoder_3_out4), .out5(decoder_3_out5), .out6(decoder_3_out6), .out7(decoder_3_out7),
    .sel(in_4[2:0]), .en(decoder_1_out1));
  Decoder #(.select(3), .disabled(0)) decoder_4 (
    .out0(decoder_4_out0), .out1(decoder_4_out1), .out2(decoder_4_out2), .out3(decoder_4_out3),
    .out4(decoder_4_out4), .out5(decoder_4_out5), .out6(decoder_4_out6), .out7(decoder_4_out7),
    .sel(in_4[2:0]), .en(decoder_1_out2));
  Decoder #(.select(3), .disabled(0)) decoder_5 (
    .out0(decoder_5_out0), .out1(decoder_5_out1), .out2(decoder_5_out2), .out3(decoder_5_out3),
    .out4(decoder_5_out4), .out5(decoder_5_out5), .out6(decoder_5_out6), .out7(decoder_5_out7),
    .sel(in_4[2:0]), .en(decoder_1_out3));
  Register #(.width(32), .trigger("falling")) u__00 (.D(in_9), .en(decoder_2_out0), .Q(_00), .clr(in_8));  // open: clk
  Register #(.width(32), .trigger("falling")) u__08 (.D(in_9), .en(decoder_3_out0), .Q(_08), .clk(in_7), .clr(in_8));
  Register #(.width(32), .trigger("falling")) u__16 (.D(in_9), .en(decoder_4_out0), .Q(_16), .clk(in_7), .clr(in_8));
  Register #(.width(32), .trigger("falling")) u__24 (.D(in_9), .en(decoder_5_out0), .Q(_24), .clk(in_7), .clr(in_8));
  Register #(.width(32), .trigger("falling")) u__01 (.D(in_9), .en(decoder_2_out1), .Q(_01), .clk(in_7), .clr(in_8));
  // Probe on _09
  Register #(.width(32), .trigger("falling")) u__09 (.D(in_9), .en(decoder_3_out1), .Q(_09), .clk(in_7), .clr(in_8));
  Register #(.width(32), .trigger("falling")) u__17 (.D(in_9), .en(decoder_4_out1), .Q(_17), .clk(in_7), .clr(in_8));
  Register #(.width(32), .trigger("falling")) u__25 (.D(in_9), .en(decoder_5_out1), .Q(_25), .clk(in_7), .clr(in_8));
  Register #(.width(32), .trigger("falling")) u__02 (.D(in_9), .en(decoder_2_out2), .Q(_02), .clk(in_7), .clr(in_8));
  // Probe on _01
  Register #(.width(32), .trigger("falling")) u__10 (.D(in_9), .en(decoder_3_out2), .Q(_10), .clk(in_7), .clr(in_8));
  Register #(.width(32), .trigger("falling")) u__18 (.D(in_9), .en(decoder_4_out2), .Q(_18), .clk(in_7), .clr(in_8));
  Register #(.width(32), .trigger("falling")) u__26 (.D(in_9), .en(decoder_5_out2), .Q(_26), .clk(in_7), .clr(in_8));
  Register #(.width(32), .trigger("falling")) u__03 (.D(in_9), .en(decoder_2_out3), .Q(_03), .clk(in_7), .clr(in_8));
  // Probe on _10
  Register #(.width(32), .trigger("falling")) u__11 (.D(in_9), .en(decoder_3_out3), .Q(_11), .clk(in_7), .clr(in_8));
  Register #(.width(32), .trigger("falling")) u__19 (.D(in_9), .en(decoder_4_out3), .Q(_19), .clk(in_7), .clr(in_8));
  Register #(.width(32), .trigger("falling")) u__27 (.D(in_9), .en(decoder_5_out3), .Q(_27), .clk(in_7), .clr(in_8));
  Register #(.width(32), .trigger("falling")) u__04 (.D(in_9), .en(decoder_2_out4), .Q(_04), .clk(in_7), .clr(in_8));
  Register #(.width(32), .trigger("falling")) u__12 (.D(in_9), .en(decoder_3_out4), .Q(_12), .clk(in_7), .clr(in_8));
  Register #(.width(32), .trigger("falling")) u__20 (.D(in_9), .en(decoder_4_out4), .Q(_20), .clk(in_7), .clr(in_8));
  Register #(.width(32), .trigger("falling")) u__28 (.D(in_9), .en(decoder_5_out4), .Q(_28), .clk(in_7), .clr(in_8));
  Register #(.width(32), .trigger("falling")) u__05 (.D(in_9), .en(decoder_2_out5), .Q(_05), .clk(in_7), .clr(in_8));
  Register #(.width(32), .trigger("falling")) u__13 (.D(in_9), .en(decoder_3_out5), .Q(_13), .clk(in_7), .clr(in_8));
  Register #(.width(32), .trigger("falling")) u__21 (.D(in_9), .en(decoder_4_out5), .Q(_21), .clk(in_7), .clr(in_8));
  Register #(.width(32), .trigger("falling")) u__29 (.D(in_9), .en(decoder_5_out5), .Q(_29), .clk(in_7), .clr(in_8));
  Register #(.width(32), .trigger("falling")) u__06 (.D(in_9), .en(decoder_2_out6), .Q(_06), .clk(in_7), .clr(in_8));
  Register #(.width(32), .trigger("falling")) u__14 (.D(in_9), .en(decoder_3_out6), .Q(_14), .clk(in_7), .clr(in_8));
  Register #(.width(32), .trigger("falling")) u__22 (.D(in_9), .en(decoder_4_out6), .Q(_22), .clk(in_7), .clr(in_8));
  Register #(.width(32), .trigger("falling")) u__30 (.D(in_9), .en(decoder_5_out6), .Q(_30), .clk(in_7), .clr(in_8));
  Register #(.width(32), .trigger("falling")) u__07 (.D(in_9), .en(decoder_2_out7), .Q(_07), .clk(in_7), .clr(in_8));
  Register #(.width(32), .trigger("falling")) u__15 (.D(in_9), .en(decoder_3_out7), .Q(_15), .clk(in_7), .clr(in_8));
  Register #(.width(32), .trigger("falling")) u__23 (.D(in_9), .en(decoder_4_out7), .Q(_23), .clk(in_7), .clr(in_8));
  Register #(.width(32), .trigger("falling")) u__31 (.D(in_9), .en(decoder_5_out7), .Q(_31), .clk(in_7), .clr(in_8));
  // Probe on _31
  Multiplexer #(.select(5), .width(32)) multiplexer_1 (
    .in0(_00), .in1(_01), .in2(_02), .in3(_03), .in4(_04), .in5(_05), .in6(_06), .in7(_07), .in8(_08),
    .in9(_09), .in10(_10), .in11(_11), .in12(_12), .in13(_13), .in14(_14), .in15(_15), .in16(_16),
    .in17(_17), .in18(_18), .in19(_19), .in20(_20), .in21(_21), .in22(_22), .in23(_23), .in24(_24),
    .in25(_25), .in26(_26), .in27(_27), .in28(_28), .in29(_29), .in30(_30), .in31(_31), .out(R1), .sel(in_1));  // open: en
  Multiplexer #(.select(5), .width(32)) multiplexer_2 (
    .in0(_00), .in1(_01), .in2(_02), .in3(_03), .in4(_04), .in5(_05), .in6(_06), .in7(_07), .in8(_08),
    .in9(_09), .in10(_10), .in11(_11), .in12(_12), .in13(_13), .in14(_14), .in15(_15), .in16(_16),
    .in17(_17), .in18(_18), .in19(_19), .in20(_20), .in21(_21), .in22(_22), .in23(_23), .in24(_24),
    .in25(_25), .in26(_26), .in27(_27), .in28(_28), .in29(_29), .in30(_30), .in31(_31), .out(R2), .sel(in_3));  // open: en

  // Other names for the same wires on the sheet: CLK = in_7; Dest_Address[4:0] = in_4; HI__in[31:0] = in_2;
  //   IN_Reg_1[4:0] = in_1; IN_Reg_2[4:0] = in_3; Input_Data[31:0] = in_9; LO__in[31:0] = in_5; Out_Reg_1[31:0] = R1;
  //   Out_Reg_2[31:0] = R2; Reset = in_8; WH___L = in_10; Write_Enable = in_6

  // Notes on the sheet:
  //   HI
  //   INPUTS
  //   OUTPUTS
  //   LO
endmodule

module ALU (
  input  [3:0] in_1,
  input  [31:0] in_2,
  input  [31:0] in_3,
  output Carry_Flag,
  output Overflow,
  output [31:0] out_6,
  output [31:0] out_7,
  output Equal,
  output Zero_Flag
);

  wire Clk, comparator_1_lt, comparator_2_lt;
  wire [1:0] adder_with_overflow_detection_1_overflow, substractor_with_overflow_detection_1_out_6;
  wire [31:0] adder_with_overflow_detection_1_out_5, and_1_out, bit_extender_1_out, bit_extender_2_out,
       divider_1_out, divider_1_rem, divider_2_out, divider_2_rem, multiplier_1_cout, multiplier_1_out,
       multiplier_2_cout, multiplier_2_out, nor_1_out, or_1_out, random_1_out, shifter_1_out, shifter_2_out,
       shifter_3_out, substractor_with_overflow_detection_1_out_5, xor_1_out;

  // Probe on in_2
  // Probe on in_3
  Adder_with_overflow_detection adder_with_overflow_detection_1 (
    .Carry_Flag(adder_with_overflow_detection_1_overflow[1]), .in_2(in_2), .in_3(in_3),
    .out_5(adder_with_overflow_detection_1_out_5), .Overflow(adder_with_overflow_detection_1_overflow[0]));  // open: Carry_in
  Substractor_with_overflow_detection substractor_with_overflow_detection_1 (
    .out_4(substractor_with_overflow_detection_1_out_6[1]), .in_1(in_2), .in_2(in_3),
    .out_5(substractor_with_overflow_detection_1_out_5),
    .out_6(substractor_with_overflow_detection_1_out_6[0]));  // open: in_3
  Clock clock_1 (.out(Clk));
  Shifter #(.width(32)) shifter_1 (.in(in_2), .\dist (in_3[4:0]), .out(shifter_1_out));
  Shifter #(.width(32), .shift("lr")) shifter_2 (.in(in_2), .\dist (in_3[4:0]), .out(shifter_2_out));
  assign and_1_out = in_2 & in_3;  // AND_Gate and_1, 32 bits wide
  Shifter #(.width(32), .shift("ar")) shifter_3 (.in(in_2), .\dist (in_3[4:0]), .out(shifter_3_out));
  assign or_1_out = in_2 | in_3;  // OR_Gate or_1, 32 bits wide
  assign nor_1_out = ~(in_2 | in_3);  // NOR_Gate nor_1, 32 bits wide
  assign xor_1_out = in_2 ^ in_3;  // XOR_Gate xor_1, 32 bits wide
  Comparator #(.width(32)) comparator_1 (.a(in_2), .b(in_3), .lt(comparator_1_lt));  // open: gt, eq
  Random #(.width(32)) random_1 (.clk(Clk), .next(1'b1), .out(random_1_out));  // open: clr
  Comparator #(.width(32), .mode("unsigned")) comparator_2 (
    .a(in_2), .b(in_3), .eq(Equal), .lt(comparator_2_lt));  // open: gt
  Multiplier #(.width(32)) multiplier_1 (
    .a(in_2), .b(in_3), .out(multiplier_1_out), .cout(multiplier_1_cout));  // open: cin
  Divider #(.width(32)) divider_1 (.a(in_2), .b(in_3), .out(divider_1_out), .rem(divider_1_rem));  // open: upper
  Multiplier #(.width(32)) multiplier_2 (
    .a(in_2), .b(in_3), .out(multiplier_2_out), .cout(multiplier_2_cout));  // open: cin
  Divider #(.width(32)) divider_2 (.a(in_2), .b(in_3), .out(divider_2_out), .rem(divider_2_rem));  // open: upper
  // Probe on in_1
  assign bit_extender_1_out = {{31{1'b0}}, comparator_1_lt};  // Bit_Extender bit_extender_1
  assign bit_extender_2_out = {{31{1'b0}}, comparator_2_lt};  // Bit_Extender bit_extender_2
  Multiplexer #(.select(4), .width(2)) multiplexer_1 (
    .in0(adder_with_overflow_detection_1_overflow), .in1(substractor_with_overflow_detection_1_out_6),
    .in2(2'b00), .in3(2'b00), .in4(2'b00), .in5(2'b00), .in6(2'b00), .in7(2'b00), .in8(2'b00), .in9(2'b00),
    .in10(2'b00), .in11(2'b00), .in12(2'b00), .in13(2'b00), .in14(2'b00), .in15(2'b00),
    .out({Overflow, Carry_Flag}), .sel(in_1));  // open: en
  // Probe on out_6
  Multiplexer #(.select(4), .width(32), .enable("false")) multiplexer_2 (
    .in0(adder_with_overflow_detection_1_out_5), .in1(substractor_with_overflow_detection_1_out_5),
    .in2(shifter_1_out), .in3(shifter_2_out), .in4(and_1_out), .in5(shifter_3_out), .in6(or_1_out),
    .in7(nor_1_out), .in8(xor_1_out), .in9(bit_extender_1_out), .in10(random_1_out),
    .in11(bit_extender_2_out), .in12(multiplier_1_out), .in13(divider_1_out), .in14(multiplier_2_out),
    .in15(divider_2_out), .out(out_6), .sel(in_1));
  Multiplexer #(.select(4), .width(32)) multiplexer_3 (
    .in0({32{1'b0}}), .in1({32{1'b0}}), .in2({32{1'b0}}), .in3({32{1'b0}}), .in4({32{1'b0}}),
    .in5({32{1'b0}}), .in6({32{1'b0}}), .in7({32{1'b0}}), .in8({32{1'b0}}), .in9({32{1'b0}}),
    .in10({32{1'b0}}), .in11({32{1'b0}}), .in12(multiplier_1_cout), .in13(divider_1_rem),
    .in14(multiplier_2_cout), .in15(divider_2_rem), .out(out_7), .sel(in_1));  // open: en
  // Probe on out_7
  Comparator #(.width(32)) comparator_3 (.a({32{1'b0}}), .b(out_6), .eq(Zero_Flag));  // open: gt, lt

  // Other names for the same wires on the sheet: CF = Carry_Flag; OF = Overflow; A[31:0] = in_2; B[31:0] = in_3;
  //   Help_Result[31:0] = out_7; Main_Result[31:0] = out_6; OP[3:0] = in_1; Zero = Zero_Flag

  // Notes on the sheet:
  //   Inputs
  //   and
  //   arithmetic right
  //   or
  //   nor
  //   xor
  //   Adder with OF
  //   substractor with OF
  //   logical left
  //   logical right
  //   less than
  //   Random generator
  //   less than (U)
  //   signed mult
  //   signed div
  //   unsigned mult
  //   unsigned div
  //   Outputs
endmodule

module ALU_Decoder (
  input  [5:0] Op_Code,
  input  [5:0] Func_Code,
  input  Sum,
  output [3:0] ALU_Operation,
  output Write_Hi___Lo
);

  wire and_5_out;
  wire [1:0] nor_1_out;
  wire [2:2] or_1_out;
  wire [3:0] and_3_out, multiplexer_1_out, multiplexer_2_out;

  and and_1 (and_3_out[3], Op_Code[3], Op_Code[1]);
  and and_2 (and_3_out[2], Op_Code[2], ~Op_Code[1]);  // AND_Gate
  and and_3 (and_3_out[0], Op_Code[3], ~Op_Code[2], Op_Code[1]);  // AND_Gate
  or or_1 (or_1_out[2], Func_Code[2], Func_Code[4]);
  Multiplexer #(.width(4), .enable("false")) multiplexer_1 (
    .in0(4'b1001), .in1({and_3_out[3:2], Op_Code[0], and_3_out[0]}), .out(multiplexer_1_out), .sel(Op_Code[3]));
  and and_4 (nor_1_out[1], Op_Code[5], Op_Code[4], Op_Code[3], ~Op_Code[2], ~Op_Code[1], ~Op_Code[0]);  // AND_Gate
  and and_5 (and_5_out, Func_Code[3], Func_Code[4], ~Func_Code[5]);  // AND_Gate
  Multiplexer #(.select(2), .width(4), .enable("false")) multiplexer_2 (
    .in0(multiplexer_1_out), .in1({Func_Code[3], or_1_out[2], Func_Code[0], Func_Code[1]}),
    .in2(Func_Code[3:0]), .in3(Func_Code[3:0]), .out(multiplexer_2_out), .sel(nor_1_out));
  Multiplexer #(.width(4), .enable("false")) multiplexer_3 (
    .in0(multiplexer_2_out), .in1(4'b0000), .out(ALU_Operation), .sel(Sum));
  nor nor_1 (nor_1_out[0], Op_Code[5], Op_Code[4], Op_Code[3], Op_Code[2], Op_Code[1], Op_Code[0], 1'b0);
  and and_6 (Write_Hi___Lo, nor_1_out[0], and_5_out);

  // Notes on the sheet:
  //   add
  //   sub
  //   logical left
  //   logical right
  //   or
  //   nor
  //   xor
  //   divu
  //   Operation
  //   pop
  //   push
  //   Operation
  //   and
  //   arithmetic right
  //   slt
  //   rnd (Op 11 1111)
  //   sltu
  //   mult
  //   div
  //   mulu
  //   Op-Code: 11 1000
  //   OP-Code: 00 0000
  //   Func code
  //   10 0000
  //   10 0001
  //   10 0010
  //   10 0011
  //   10 0100
  //   10 0101
  //   10 0110
  //   10 0111
  //   10 1000
  //   10 1001
  //   10 1010
  //   10 1011
  //   10 1100
  //   10 1101
  //   10 1110
  //   10 1111
  //   ALU Op
  //   0000
  //   0001
  //   ALU Op
  //   0000
  //   0001
  //   0010
  //   0011
  //   0100
  //   0101
  //   0110
  //   0111
  //   1000
  //   1001
  //   1010
  //   1011
  //   1100
  //   1101
  //   1110
  //   1111
  //   ALU Op: 1001
  //   Operation
  //   beq
  //   bne
  //   blez
  //   bgtz
  //   bltz
  //   Operation
  //   addi
  //   andi
  //   ori
  //   xori
  //   slti
  //   sltiu
  //   Op code
  //   00 0100
  //   00 0101
  //   00 0110
  //   00 0111
  //   00 0001
  //   Op code
  //   00 1000
  //   00 1100
  //   00 1101
  //   00 1110
  //   00 1010
  //   00 1011
  //   ALU Op
  //   0000
  //   0100
  //   0110
  //   1000
  //   1001
  //   1011
endmodule

module Instruction_decoder (
  input  [31:0] Instruction,
  input  Write_Instruction,
  input  Clock,
  input  Reset,
  input  [31:0] Program_Counter__updated,
  output Write_Rd,
  output jmp,
  output [15:0] Offset,
  output nRead_Write,
  output [5:0] Op_Code,
  output [1:0] Jump_Value_Selector,
  output [4:0] Rs,
  output [5:0] Func_Code,
  output [4:0] Rt,
  output [4:0] Rd,
  output [31:0] Jump_Value,
  output Inmediate,
  output nHi_Lo,
  output [2:0] Operation_Type,
  output nPush_Pop,
  output nRead_Write_Memory,
  output [2:0] Jump_Type
);

  wire and_3_out, and_4_out, and_5_out, and_6_out, and_9_out, demultiplexer_1_out0, demultiplexer_1_out1,
       Halt, IO, J_Type, jmp_t, Memory_Op, Move_Hi_Lo, nand_1_out, NOP, nor_2_out, nor_4_out, nor_6_out,
       nor_7_out, nor_8_out, or_2_out, or_4_out, or_5_out, Stack, xor_1_out;

  and and_1 (Move_Hi_Lo, Write_Rd, ~Func_Code[3], Func_Code[4], ~Func_Code[5]);  // AND_Gate
  and and_2 (Memory_Op, Op_Code[0], Op_Code[1], ~Op_Code[4], Op_Code[5]);  // AND_Gate
  Register #(.width(32), .trigger("falling")) Instruction_Memory (
    .D(Instruction), .en(Write_Instruction), .Q({Op_Code, Rs, Rt, Offset[15:6], Func_Code}), .clk(Clock),
    .clr(Reset));
  xor xor_1 (xor_1_out, Op_Code[3], Op_Code[5]);
  // Probe on Rs
  // Probe on Rt
  // Probe on Offset[15:11]
  nor nor_1 (Inmediate, ~Op_Code[3], Op_Code[4], Op_Code[5]);  // NOR_Gate
  not not_1 (nHi_Lo, Func_Code[1]);
  not not_2 (nPush_Pop, Func_Code[0]);
  Multiplexer #(.enable("false")) multiplexer_1 (
    .in0(Op_Code[3]), .in1(Func_Code[0]), .out(nRead_Write_Memory), .sel(Write_Rd));
  or or_1 (nRead_Write, Write_Rd, xor_1_out);
  or or_2 (or_2_out, Inmediate, nor_2_out);
  nor nor_2 (nor_2_out, Move_Hi_Lo, NOP);
  Demultiplexer #(.enable("false")) demultiplexer_1 (
    .out0(demultiplexer_1_out0), .out1(demultiplexer_1_out1), .in(IO), .sel(Func_Code[2]));
  nor nor_3 (NOP, Func_Code[0], Func_Code[1], Func_Code[2], Func_Code[3], Func_Code[4], Func_Code[5], Offset[6], Offset[7], Offset[8], Offset[9], Offset[10], Offset[11], Offset[12], Offset[13], Offset[14], Offset[15], Rt[1], Rt[2], Rt[3], Rt[4], Rs[0], Rs[1], Rs[2], Rs[3], Rs[4], Op_Code[0], Op_Code[1], Op_Code[2], Op_Code[3], Op_Code[4], Op_Code[5], Rt[0]);
  Priority_Encoder priority_encoder_1 (
    .in0(or_2_out), .in1(jmp_t), .in2(Memory_Op), .in3(Move_Hi_Lo), .in4(Stack), .in5(demultiplexer_1_out0),
    .in6(demultiplexer_1_out1), .in7(Halt), .out(Operation_Type));  // open: en_in, gs, en_out
  and and_3 (and_3_out, Op_Code[5], Op_Code[4]);
  nor nor_4 (nor_4_out, Op_Code[5], Op_Code[4], Op_Code[3], Op_Code[2], Op_Code[1], Op_Code[0]);
  nor nor_5 (J_Type, Op_Code[0], ~Op_Code[1], Op_Code[2], Op_Code[3], Op_Code[4], Op_Code[5]);  // NOR_Gate
  or or_3 (Write_Rd, and_3_out, nor_4_out);
  nand nand_1 (nand_1_out, ~Op_Code[0], Op_Code[1], ~Op_Code[2]);  // NAND_Gate
  or or_4 (or_4_out, Op_Code[0], Op_Code[1], Op_Code[2]);
  nor nor_6 (nor_6_out, Op_Code[3], Op_Code[4], Op_Code[5]);
  nor nor_7 (nor_7_out, Op_Code[0], Op_Code[1], Op_Code[2]);
  and and_4 (and_4_out, Op_Code[0], Op_Code[1], Op_Code[2]);
  and and_5 (and_5_out, Op_Code[3], Op_Code[4], Op_Code[5]);
  and and_6 (and_6_out, Func_Code[0], Func_Code[1], Func_Code[3], Func_Code[4], Func_Code[5]);
  or or_5 (or_5_out, Func_Code[2], Func_Code[0]);
  and and_7 (Jump_Value_Selector[0], nand_1_out, or_4_out, nor_6_out);
  and and_8 (Stack, nor_7_out, and_5_out);
  and and_9 (and_9_out, and_4_out, and_5_out);
  and and_10 (Halt, and_9_out, and_6_out);
  and and_11 (IO, and_9_out, or_5_out);
  or or_6 (jmp, J_Type, Jump_Value_Selector[1], Jump_Value_Selector[0]);
  Multiplexer #(.width(3), .enable("false")) multiplexer_2 (
    .in0(Op_Code[2:0]), .in1(3'b000), .out(Jump_Type), .sel(J_Type));
  or or_7 (jmp_t, NOP, jmp);
  Multiplexer #(.width(32), .enable("false")) multiplexer_3 (
    .in0(Program_Counter__updated),
    .in1({Program_Counter__updated[31:28], Rs, Rt, Offset[15:6], Func_Code, 2'b00}), .out(Jump_Value),
    .sel(J_Type));
  and and_12 (Jump_Value_Selector[1], nor_4_out, nor_8_out);
  nor nor_8 (nor_8_out, Func_Code[0], Func_Code[1], Func_Code[2], ~Func_Code[3], Func_Code[4], Func_Code[5]);  // NOR_Gate

  assign Offset[5:0] = Func_Code;
  assign Rd = Offset[15:11];

  // Other names for the same wires on the sheet: Instruction_t[31:0] = {Op_Code, Rs, Rt, Offset[15:6], Func_Code};
  //   PC[31:0] = Program_Counter__updated; Branch = Jump_Value_Selector[0]; JR = Jump_Value_Selector[1];
  //   R_Type = Write_Rd

  // Notes on the sheet:
  //   Inputs
  //   Register File
  //   En el register file paso como selector del registro a escribir un multiplexer
  //   con con Rt y Rd de entradas y este bit (R-Type) como selector
  //   Control Unit
  //   MISC
  //   Common
  //   OUTPUTS
  //   Branch Control
  //   En el branch control se pasa el jump value, el offsett trabajado y
  //   el contenido de Rs por un multiplexer con este selector
  //   Si es nop se mantiene el PC, si no se construye la nueva direccion
  //   Selector que usara el branch control
  //   para determinar el tipo de salto
endmodule

module Branch_Control (
  input  Jump_Operation,
  input  [31:0] Jump_Value,
  input  [2:0] Jump_Selector,
  input  [31:0] Next_Program_Counter_Value,
  input  Clock,
  input  ALU_Less,
  input  Try_Jump,
  input  ALU_Equals,
  input  Update_PC,
  input  Reset,
  output [31:0] Program_Counter,
  output out_12
);

  wire and_1_out, and_2_out, and_3_out, multiplexer_2_out, not_1_out, not_2_out, or_1_out, or_2_out;
  wire [31:0] multiplexer_1_out;

  Multiplexer #(.width(32), .enable("false")) multiplexer_1 (
    .in0(Next_Program_Counter_Value), .in1(Jump_Value), .out(multiplexer_1_out), .sel(and_2_out));
  and and_1 (and_1_out, and_2_out, Try_Jump);
  and and_2 (and_2_out, Jump_Operation, multiplexer_2_out);
  Multiplexer #(.select(3), .enable("false")) multiplexer_2 (
    .in0(1'b1), .in1(ALU_Less), .in2(1'b1), .in3(1'b0), .in4(ALU_Equals), .in5(not_1_out), .in6(or_2_out),
    .in7(not_2_out), .out(multiplexer_2_out), .sel(Jump_Selector));
  Register #(.width(32), .trigger("falling")) PC (
    .D(multiplexer_1_out), .en(or_1_out), .Q(Program_Counter), .clk(Clock), .clr(Reset));
  or or_1 (or_1_out, and_1_out, Update_PC);
  not not_1 (not_1_out, ALU_Equals);
  not not_2 (not_2_out, or_2_out);
  and and_3 (and_3_out, ~Jump_Selector[1], Jump_Selector[2]);  // AND_Gate
  or or_2 (or_2_out, ALU_Less, ALU_Equals);
  and and_4 (out_12, ~and_3_out, Jump_Operation);  // AND_Gate

  // Other names for the same wires on the sheet: CLK = Clock; Equals = ALU_Equals; Imp = Jump_Operation;
  //   Jump_S[2:0] = Jump_Selector; Jump_V[31:0] = Jump_Value; Less = ALU_Less; PC[31:0] = Next_Program_Counter_Value;
  //   Update = Update_PC

  // Notes on the sheet:
  //   INPUTS
  //   OUTPUT
endmodule

module Access_Memory (
  input  [31:0] Target_Address,
  input  [31:0] Ram_O0,
  input  [31:0] Ram_O1,
  input  [31:0] To_Write,
  input  [31:0] Ram_O2,
  input  [31:0] Ram_O3,
  output [15:0] Address,
  output [3:0] Mask,
  output [31:0] Ram_I0,
  output [31:0] Ram_I1,
  output [31:0] Ram_out,
  output [31:0] Ram_I2,
  output [31:0] Ram_I3
);

  wire [31:0] divider_1_out;
  wire [31:16] divider_2_out;

  Multiplexer #(.select(2), .width(32), .enable("false")) multiplexer_1 (
    .in0(Ram_O0), .in1(Ram_O1), .in2(Ram_O2), .in3(Ram_O3),
    .out({Ram_out[7:0], Ram_out[15:8], Ram_out[23:16], Ram_out[31:24]}), .sel(divider_1_out[1:0]));
  Divider #(.width(32)) divider_1 (.a(Target_Address), .b(32'h4), .out(divider_1_out));  // open: upper, rem
  Decoder #(.select(2), .enable("false")) decoder_1 (
    .out0(Mask[0]), .out1(Mask[1]), .out2(Mask[2]), .out3(Mask[3]), .sel(divider_1_out[1:0]));
  Divider #(.width(32)) divider_2 (.a(divider_1_out), .b(32'h4), .out({divider_2_out, Address}));  // open: upper, rem

  assign Ram_I0 = {To_Write[7:0], To_Write[15:8], To_Write[23:16], To_Write[31:24]};
  assign Ram_I1 = {To_Write[7:0], To_Write[15:8], To_Write[23:16], To_Write[31:24]};
  assign Ram_I2 = {To_Write[7:0], To_Write[15:8], To_Write[23:16], To_Write[31:24]};
  assign Ram_I3 = {To_Write[7:0], To_Write[15:8], To_Write[23:16], To_Write[31:24]};
endmodule

module Chronometer (
  input  INPUTS,
  input  in_2,
  input  [3:0] in_3,
  input  in_4,
  output out_5,
  output out_6
);

  wire comparator_2_eq, d_ff_1_q, or_1_out;
  wire [4:0] counter_1_q;

  Counter #(.width(5), .max('h1f)) counter_1 (
    .load(1'b0), .count(in_2), .Q(counter_1_q), .clk(INPUTS), .clr(or_1_out));  // open: D, carry
  Comparator #(.width(5)) comparator_1 (.a({1'b0, in_3}), .b(counter_1_q), .eq(out_6));  // open: gt, lt
  Comparator #(.width(5)) comparator_2 (.a(counter_1_q), .b({5{1'b0}}), .eq(comparator_2_eq));  // open: gt, lt
  or or_1 (or_1_out, d_ff_1_q, in_4);
  D_Flip_Flop #(.trigger("falling")) d_ff_1 (
    .clk(INPUTS), .D(out_6), .Q(d_ff_1_q), .reset(or_1_out));  // open: Qn, preset, en
  or or_2 (out_5, ~comparator_2_eq, in_2);  // OR_Gate

  // Other names for the same wires on the sheet: Frecuency[3:0] = in_3; Clock = INPUTS; Counting = out_5; END = out_6;
  //   Reset_Signal = in_4; Start_Signal = in_2

  // Notes on the sheet:
  //   OUTPUTS
endmodule

module Cache (
  input  [31:0] Data_From_RAM_0,
  input  [31:0] Data_From_RAM_2,
  input  [31:0] Data_From_RAM_1,
  input  [31:0] Data_From_RAM_3,
  input  [31:0] Address,
  input  Read,
  input  CLK,
  input  RST,
  input  Ram_Read_Finish,
  input  Ram_Write,
  output [31:0] Data_Out,
  output Miss_Hit
);

  wire and_9_out, and_10_out, and_11_out, and_12_out, and_13_out, and_14_out, and_15_out, and_16_out,
       and_25_out, and_26_out, and_27_out, and_28_out, and_29_out, and_30_out, and_31_out, and_32_out, ClV0,
       ClV1, ClV2, ClV3, ClV4, ClV5, ClV6, ClV7, E_0, E_1, E_2, E_3, E_5, E_6, E_7, Line_0, Line_1, Line_2,
       Line_3, Line_4, Line_5, Line_6, Line_7, Match_Data_0, Match_Data_1, Match_Data_2, Match_Data_3,
       Match_Data_4, Match_Data_5, Match_Data_6, Match_Data_7, Match_Tag_0, Match_Tag_1, Match_Tag_2,
       Match_Tag_3, Match_Tag_4, Match_Tag_5, Match_Tag_6, Match_Tag_7, or_9_out, V0, V1, V2, V3, V4, V5, V6,
       V7;
  wire [25:0] Tag, Tag_0, Tag_1, Tag_2, Tag_3, Tag_4, Tag_5, Tag_6, Tag_7;
  wire [31:0] _000000, _000001, _000010, _000011, _000100, _000101, _000110, _000111, _001000, _001001,
       _001010, _001011, _001100, _001101, _001110, _001111, _010000, _010001, _010010, _010011, _010100,
       _010101, _010110, _010111, _011000, _011001, _011010, _011011, _011100, _011101, _011110, _011111,
       Out_00, Out_01, Out_10, Out_11;

  Register #(.width(26)) u_Tag_0 (.D(Tag), .en(E_0), .Q(Tag_0), .clk(CLK), .clr(RST));
  Register #(.width(26)) u_Tag_1 (.D(Tag), .en(E_1), .Q(Tag_1), .clk(CLK), .clr(RST));
  Register #(.width(26)) u_Tag_2 (.D(Tag), .en(E_2), .Q(Tag_2), .clk(CLK), .clr(RST));
  Register #(.width(26)) u_Tag_3 (.D(Tag), .en(E_3), .Q(Tag_3), .clk(CLK), .clr(RST));
  Register #(.width(26)) u_Tag_4 (.D(Tag), .en(CLK), .Q(Tag_4), .clk(CLK), .clr(RST));
  Register #(.width(26)) u_Tag_5 (.D(Tag), .en(E_5), .Q(Tag_5), .clk(CLK), .clr(RST));
  Register #(.width(26)) u_Tag_6 (.D(Tag), .en(E_6), .Q(Tag_6), .clk(CLK), .clr(RST));
  Register #(.width(26)) u_Tag_7 (.D(Tag), .en(E_7), .Q(Tag_7), .clk(CLK), .clr(RST));
  assign Tag = {{1{Address[31]}}, Address[31:7]};  // Bit_Extender bit_extender_1
  Register #(.width(32)) register_1 (.D(Data_From_RAM_3), .en(E_0), .Q(_000011), .clk(CLK), .clr(RST));
  Register #(.width(32)) register_2 (.D(Data_From_RAM_3), .en(E_1), .Q(_000111), .clk(CLK), .clr(RST));
  Register #(.width(32)) register_3 (.D(Data_From_RAM_3), .en(E_2), .Q(_001011), .clk(CLK), .clr(RST));
  Register #(.width(32)) register_4 (.D(Data_From_RAM_3), .en(E_3), .Q(_001111), .clk(CLK), .clr(RST));
  Register #(.width(32)) register_5 (.D(Data_From_RAM_3), .en(CLK), .Q(_010011), .clk(CLK), .clr(RST));
  Register #(.width(32)) register_6 (.D(Data_From_RAM_3), .en(E_5), .Q(_010111), .clk(CLK), .clr(RST));
  Register #(.width(32)) register_7 (.D(Data_From_RAM_3), .en(E_6), .Q(_011011), .clk(CLK), .clr(RST));
  Register #(.width(32)) register_8 (.D(Data_From_RAM_3), .en(E_7), .Q(_011111), .clk(CLK), .clr(RST));
  Register #(.width(32)) register_9 (.D(Data_From_RAM_2), .en(E_0), .Q(_000010), .clk(CLK), .clr(RST));
  Register #(.width(32)) register_10 (.D(Data_From_RAM_2), .en(E_1), .Q(_000110), .clk(CLK), .clr(RST));
  Register #(.width(32)) register_11 (.D(Data_From_RAM_2), .en(E_2), .Q(_001010), .clk(CLK), .clr(RST));
  Register #(.width(32)) register_12 (.D(Data_From_RAM_2), .en(E_3), .Q(_001110), .clk(CLK), .clr(RST));
  Register #(.width(32)) register_13 (.D(Data_From_RAM_2), .en(CLK), .Q(_010010), .clk(CLK), .clr(RST));
  Register #(.width(32)) register_14 (.D(Data_From_RAM_2), .en(E_5), .Q(_010110), .clk(CLK), .clr(RST));
  Register #(.width(32)) register_15 (.D(Data_From_RAM_2), .en(E_6), .Q(_011010), .clk(CLK), .clr(RST));
  Register #(.width(32)) register_16 (.D(Data_From_RAM_2), .en(E_7), .Q(_011110), .clk(CLK), .clr(RST));
  and and_1 (E_0, Ram_Read_Finish, Line_0);
  and and_2 (E_1, Ram_Read_Finish, Line_1);
  and and_3 (E_2, Ram_Read_Finish, Line_2);
  and and_4 (E_3, Ram_Read_Finish, Line_3);
  Register #(.width(32)) register_17 (.D(Data_From_RAM_1), .en(E_0), .Q(_000001), .clk(CLK), .clr(RST));
  Register #(.width(32)) register_18 (.D(Data_From_RAM_1), .en(E_1), .Q(_000101), .clk(CLK), .clr(RST));
  Register #(.width(32)) register_19 (.D(Data_From_RAM_1), .en(E_2), .Q(_001001), .clk(CLK), .clr(RST));
  Register #(.width(32)) register_20 (.D(Data_From_RAM_1), .en(E_3), .Q(_001101), .clk(CLK), .clr(RST));
  Register #(.width(32)) register_21 (.D(Data_From_RAM_1), .en(CLK), .Q(_010001), .clk(CLK), .clr(RST));
  Register #(.width(32)) register_22 (.D(Data_From_RAM_1), .en(E_5), .Q(_010101), .clk(CLK), .clr(RST));
  Register #(.width(32)) register_23 (.D(Data_From_RAM_1), .en(E_6), .Q(_011001), .clk(CLK), .clr(RST));
  Register #(.width(32)) register_24 (.D(Data_From_RAM_1), .en(E_7), .Q(_011101), .clk(CLK), .clr(RST));
  Register #(.width(32)) register_25 (.D(Data_From_RAM_0), .en(E_0), .Q(_000000), .clk(CLK), .clr(RST));
  Register #(.width(32)) register_26 (.D(Data_From_RAM_0), .en(E_1), .Q(_000100), .clk(CLK), .clr(RST));
  Register #(.width(32)) register_27 (.D(Data_From_RAM_0), .en(E_2), .Q(_001000), .clk(CLK), .clr(RST));
  Register #(.width(32)) register_28 (.D(Data_From_RAM_0), .en(E_3), .Q(_001100), .clk(CLK), .clr(RST));
  Register #(.width(32)) register_29 (.D(Data_From_RAM_0), .en(CLK), .Q(_010000), .clk(CLK), .clr(RST));
  Register #(.width(32)) register_30 (.D(Data_From_RAM_0), .en(E_5), .Q(_010100), .clk(CLK), .clr(RST));
  Register #(.width(32)) register_31 (.D(Data_From_RAM_0), .en(E_6), .Q(_011000), .clk(CLK), .clr(RST));
  Register #(.width(32)) register_32 (.D(Data_From_RAM_0), .en(E_7), .Q(_011100), .clk(CLK), .clr(RST));
  Decoder #(.select(3), .enable("false")) decoder_1 (
    .out0(Line_0), .out1(Line_1), .out2(Line_2), .out3(Line_3), .out4(Line_4), .out5(Line_5), .out6(Line_6),
    .out7(Line_7), .sel(Address[6:4]));
  and and_5 (CLK, Ram_Read_Finish, Line_4);
  and and_6 (E_5, Ram_Read_Finish, Line_5);
  and and_7 (E_6, Ram_Read_Finish, Line_6);
  and and_8 (E_7, Ram_Read_Finish, Line_7);
  Comparator #(.width(26)) comparator_1 (.a(Tag), .b(Tag_0), .eq(Match_Tag_0));  // open: gt, lt
  Comparator #(.width(26)) comparator_2 (.a(Tag), .b(Tag_1), .eq(Match_Tag_1));  // open: gt, lt
  Comparator #(.width(26)) comparator_3 (.a(Tag), .b(Tag_2), .eq(Match_Tag_2));  // open: gt, lt
  Comparator #(.width(26)) comparator_4 (.a(Tag), .b(Tag_3), .eq(Match_Tag_3));  // open: gt, lt
  Comparator #(.width(26)) comparator_5 (.a(Tag), .b(Tag_4), .eq(Match_Tag_4));  // open: gt, lt
  Comparator #(.width(26)) comparator_6 (.a(Tag), .b(Tag_5), .eq(Match_Tag_5));  // open: gt, lt
  Comparator #(.width(26)) comparator_7 (.a(Tag), .b(Tag_6), .eq(Match_Tag_6));  // open: gt, lt
  Comparator #(.width(26)) comparator_8 (.a(Tag), .b(Tag_7), .eq(Match_Tag_7));  // open: gt, lt
  and and_9 (and_9_out, Match_Data_0, Ram_Write);
  and and_10 (and_10_out, Match_Data_1, Ram_Write);
  and and_11 (and_11_out, Match_Data_2, Ram_Write);
  and and_12 (and_12_out, Match_Data_3, Ram_Write);
  and and_13 (and_13_out, Match_Data_4, Ram_Write);
  and and_14 (and_14_out, Match_Data_5, Ram_Write);
  and and_15 (and_15_out, Match_Data_6, Ram_Write);
  and and_16 (and_16_out, Match_Data_7, Ram_Write);
  Bit_Validation bit_validation_1 (.CLK(CLK), .IN(E_0), .Output(V0), .RST(ClV0));
  Bit_Validation bit_validation_2 (.CLK(CLK), .IN(E_1), .Output(V1), .RST(ClV1));
  Bit_Validation bit_validation_3 (.CLK(CLK), .IN(E_2), .Output(V2), .RST(ClV2));
  Bit_Validation bit_validation_4 (.CLK(CLK), .IN(E_3), .Output(V3), .RST(ClV3));
  Bit_Validation bit_validation_5 (.CLK(CLK), .IN(CLK), .Output(V4), .RST(ClV4));
  Bit_Validation bit_validation_6 (.CLK(CLK), .IN(E_5), .Output(V5), .RST(ClV5));
  Bit_Validation bit_validation_7 (.CLK(CLK), .IN(E_6), .Output(V6), .RST(ClV6));
  Bit_Validation bit_validation_8 (.CLK(CLK), .IN(E_7), .Output(V7), .RST(ClV7));
  or or_1 (ClV0, RST, and_9_out);
  or or_2 (ClV1, RST, and_10_out);
  or or_3 (ClV2, RST, and_11_out);
  or or_4 (ClV3, RST, and_12_out);
  or or_5 (ClV4, RST, and_13_out);
  or or_6 (ClV5, RST, and_14_out);
  or or_7 (ClV6, RST, and_15_out);
  or or_8 (ClV7, RST, and_16_out);
  Multiplexer #(.select(3), .width(32)) multiplexer_1 (
    .in0(_000000), .in1(_000100), .in2(_001000), .in3(_001100), .in4(_010000), .in5(_010100), .in6(_011000),
    .in7(_011100), .out(Out_00), .sel(Address[6:4]), .en(Miss_Hit));
  Multiplexer #(.select(3), .width(32)) multiplexer_2 (
    .in0(_000001), .in1(_000101), .in2(_001001), .in3(_001101), .in4(_010001), .in5(_010101), .in6(_011001),
    .in7(_011101), .out(Out_01), .sel(Address[6:4]), .en(Miss_Hit));
  and and_17 (Match_Data_0, Match_Tag_0, Line_0);
  and and_18 (Match_Data_1, Match_Tag_1, Line_1);
  and and_19 (Match_Data_2, Match_Tag_2, Line_2);
  and and_20 (Match_Data_3, Match_Tag_3, Line_3);
  and and_21 (Match_Data_4, Match_Tag_4, Line_4);
  and and_22 (Match_Data_5, Match_Tag_5, Line_5);
  and and_23 (Match_Data_6, Match_Tag_6, Line_6);
  and and_24 (Match_Data_7, Match_Tag_7, Line_7);
  and and_25 (and_25_out, Match_Data_0, V0);
  and and_26 (and_26_out, Match_Data_1, V1);
  and and_27 (and_27_out, Match_Data_2, V2);
  and and_28 (and_28_out, Match_Data_3, V3);
  and and_29 (and_29_out, Match_Data_4, V4);
  and and_30 (and_30_out, Match_Data_5, V5);
  and and_31 (and_31_out, Match_Data_6, V6);
  and and_32 (and_32_out, Match_Data_7, V7);
  Multiplexer #(.select(2), .width(32), .enable("false")) multiplexer_3 (
    .in0(Out_00), .in1(Out_01), .in2(Out_10), .in3(Out_11), .out(Data_Out), .sel(Address[3:2]));
  or or_9 (or_9_out, and_25_out, and_26_out, and_27_out, and_28_out, and_29_out, and_30_out, and_31_out, and_32_out);
  and and_33 (Miss_Hit, or_9_out, Read);
  Multiplexer #(.select(3), .width(32)) multiplexer_4 (
    .in0(_000010), .in1(_000110), .in2(_001010), .in3(_001110), .in4(_010010), .in5(_010100), .in6(_011010),
    .in7(_011110), .out(Out_10), .sel(Address[6:4]), .en(Miss_Hit));
  Multiplexer #(.select(3), .width(32)) multiplexer_5 (
    .in0(_000011), .in1(_000111), .in2(_001011), .in3(_001111), .in4(_010011), .in5(_010111), .in6(_011011),
    .in7(_011111), .out(Out_11), .sel(Address[6:4]), .en(Miss_Hit));

  // Other names for the same wires on the sheet: Offset[1:0] = Address[3:2]; Index[2:0] = Address[6:4];
  //   Data_to_CPU[31:0] = Data_Out; Hit = Miss_Hit; In_00[31:0] = Data_From_RAM_0; In_01[31:0] = Data_From_RAM_1;
  //   In_10[31:0] = Data_From_RAM_2; In_11[31:0] = Data_From_RAM_3; T_0 = E_0; T_1 = E_1; T_2 = E_2; T_3 = E_3;
  //   E_4 = CLK; T_4 = CLK; T_5 = E_5; T_6 = E_6; T_7 = E_7

  // Notes on the sheet:
  //   Inputs
  //   Outputs
endmodule

module Inversor (
  input  [31:0] Data_In,
  output [31:0] Data_Out
);


  assign Data_Out = {Data_In[7:0], Data_In[15:8], Data_In[23:16], Data_In[31:24]};
endmodule

module Bit_Validation (
  input  CLK,
  input  IN,
  input  RST,
  output Output
);

  wire and_1_out, d_ff_1_qn;

  and and_1 (and_1_out, IN, d_ff_1_qn);
  D_Flip_Flop #(.trigger("falling")) d_ff_1 (
    .clk(CLK), .D(and_1_out), .Q(Output), .Qn(d_ff_1_qn), .en(d_ff_1_qn), .reset(RST));  // open: preset
endmodule

module Adder_with_overflow_detection (
  input  Carry_in,
  input  [31:0] in_2,
  input  [31:0] in_3,
  output Carry_Flag,
  output [31:0] out_5,
  output Overflow
);

  wire adder_1_cout;

  // Probe on in_2
  Adder #(.width(31)) adder_1 (.a(in_2[30:0]), .b(in_3[30:0]), .out(out_5[30:0]), .cin(Carry_in), .cout(adder_1_cout));
  Adder #(.width(1)) adder_2 (.a(in_2[31]), .b(in_3[31]), .out(out_5[31]), .cin(adder_1_cout), .cout(Carry_Flag));
  // Probe on in_3
  xor xor_1 (Overflow, adder_1_cout, Carry_Flag);
  // Probe on out_5

  // Other names for the same wires on the sheet: A[31:0] = in_2; B[31:0] = in_3; c_in = Carry_in; CF = Carry_Flag;
  //   OF = Overflow; Result[31:0] = out_5

  // Notes on the sheet:
  //   Inputs
  //   Outputs
endmodule

module Substractor_with_overflow_detection (
  input  [31:0] in_1,
  input  [31:0] in_2,
  input  in_3,
  output out_4,
  output [31:0] out_5,
  output out_6
);

  wire subtractor_1_bout;

  // Probe on in_1
  Subtractor #(.width(31)) subtractor_1 (
    .a(in_1[30:0]), .b(in_2[30:0]), .out(out_5[30:0]), .bin(in_3), .bout(subtractor_1_bout));
  Subtractor #(.width(1)) subtractor_2 (
    .a(in_1[31]), .b(in_2[31]), .out(out_5[31]), .bin(subtractor_1_bout), .bout(out_4));
  // Probe on in_2
  xor xor_1 (out_6, subtractor_1_bout, out_4);
  // Probe on out_5

  // Other names for the same wires on the sheet: A[31:0] = in_1; B[31:0] = in_2; b_in = in_3; CF = out_4; OF = out_6;
  //   Result[31:0] = out_5

  // Notes on the sheet:
  //   Inputs
  //   Outputs
endmodule

module _16_to_32_bit_extender (
  input  [15:0] In,
  output [31:0] Out,
  output [31:0] Outx4
);

  // Probe on In
  // Probe on {{17{In[15]}}, In[14:0]}
  // Probe on {{15{In[15]}}, In[14:0], 2'b00}

  assign Out = {{17{In[15]}}, In[14:0]};
  assign Outx4 = {{15{In[15]}}, In[14:0], 2'b00};
endmodule
